# Fritzing sketch hc-sr04 (saved by Fritzing 0.9.3b)
breadboards: 1

parts:
  R1 = Resistor [tolerance=±5% resistance=330 package="0603 [SMD]"]
  R2 = Resistor [tolerance=±5% resistance=470 package="0603 [SMD]"]  # not connected
  HC-SR04_Sensor_2 = HC-SR04 Ultrasonic Distance Sensor
  LED1 = LED - 5mm [color="Red (633nm)" package="5 mm [THT]"]
  Raspberry_Pi_1 = Raspberry Pi 3 [part_number=RPI-3-V1.2]

nets:
  N1: R1.Pin_0, HC-SR04_Sensor_2.ECHO
  N2: R1.Pin_1, Raspberry_Pi_1.GIPO24
  VCC: HC-SR04_Sensor_2.VCC, LED1.cathode, Raspberry_Pi_1.5V
  N3: HC-SR04_Sensor_2.TRIG, Raspberry_Pi_1.GIPO18
  GND: HC-SR04_Sensor_2.GND, Raspberry_Pi_1.GND
  N4: LED1.anode, Raspberry_Pi_1.GIPO17
